// Logisim project Ex1.circ as structural Verilog: 1 circuit, main circuit main
module main (
  input  in_1,
  input  in_2,
  input  in_3,
  input  in_4,
  input  in_5,
  input  [1:0] in_6,
  input  in_7,
  output out_8,
  output out_9,
  output out_10,
  output out_11
);

  wire demultiplexer_1_out0, demultiplexer_1_out1, demultiplexer_1_out2, demultiplexer_2_out0,
       demultiplexer_2_out1, demultiplexer_2_out2, demultiplexer_3_out0, demultiplexer_3_out1,
       demultiplexer_3_out2, demultiplexer_4_out0, demultiplexer_4_out1, demultiplexer_4_out2, INC_a_2,
       INC_b_2, INC_c_2, INC_d_2, main_1_a_2, main_1_b_2, main_1_c_2, main_1_d_2, main_2_out_5, main_2_out_6,
       main_2_out_7, main_2_out_8, todos_1_out_5, todos_1_out_6, todos_1_out_7, todos_1_out_8, todos_1_out_9,
       todos_1_out_10, todos_1_out_11, todos_2_out_5, todos_2_out_6, todos_2_out_7, todos_2_out_8,
       todos_2_out_9, todos_2_out_10, todos_2_out_11;

  TODOS todos_1 (
    .A(in_1), .B(in_2), .C(in_3), .D(in_4), .out_5(todos_1_out_5), .out_6(todos_1_out_6),
    .out_7(todos_1_out_7), .out_8(todos_1_out_8), .out_9(todos_1_out_9), .out_10(todos_1_out_10),
    .out_11(todos_1_out_11));
  Demultiplexer #(.select(2)) demultiplexer_1 (
    .out0(demultiplexer_1_out0), .out1(demultiplexer_1_out1), .out2(demultiplexer_1_out2), .in(in_1),
    .sel(in_6));  // open: out3, en
  Demultiplexer #(.select(2)) demultiplexer_2 (
    .out0(demultiplexer_2_out0), .out1(demultiplexer_2_out1), .out2(demultiplexer_2_out2), .in(in_2),
    .sel(in_6));  // open: out3, en
  Demultiplexer #(.select(2)) demultiplexer_3 (
    .out0(demultiplexer_3_out0), .out1(demultiplexer_3_out1), .out2(demultiplexer_3_out2), .in(in_3),
    .sel(in_6));  // open: out3, en
  Demultiplexer #(.select(2)) demultiplexer_4 (
    .out0(demultiplexer_4_out0), .out1(demultiplexer_4_out1), .out2(demultiplexer_4_out2), .in(in_4),
    .sel(in_6));  // open: out3, en
  _7_Segment_Display #(.active("false")) u_7_segment_display_1 (
    .g(todos_1_out_11), .f(todos_1_out_10), .a(todos_1_out_5), .b(todos_1_out_6), .e(todos_1_out_9),
    .d(todos_1_out_8), .c(todos_1_out_7));  // open: dp
  INC_main INC (
    .A(demultiplexer_1_out0), .B(demultiplexer_2_out0), .C(demultiplexer_3_out0), .D(demultiplexer_4_out0),
    .A_2(INC_a_2), .B_2(INC_b_2), .C_2(INC_c_2), .D_2(INC_d_2));
  NEG_main main_1 (
    .A(demultiplexer_1_out1), .B(demultiplexer_2_out1), .C(demultiplexer_3_out1), .D(demultiplexer_4_out1),
    .A_2(main_1_a_2), .B_2(main_1_b_2), .C_2(main_1_c_2), .D_2(main_1_d_2));
  DEC_main main_2 (
    .A(demultiplexer_1_out2), .B(demultiplexer_2_out2), .C(demultiplexer_3_out2), .D(demultiplexer_4_out2),
    .out_5(main_2_out_5), .out_6(main_2_out_6), .out_7(main_2_out_7), .out_8(main_2_out_8));
  Multiplexer #(.select(2)) multiplexer_1 (
    .in0(INC_a_2), .in1(main_1_a_2), .in2(main_2_out_5), .in3(in_7), .out(out_8), .sel(in_6), .en(in_5));
  Multiplexer #(.select(2)) multiplexer_2 (
    .in0(INC_b_2), .in1(main_1_b_2), .in2(main_2_out_6), .in3(in_7), .out(out_9), .sel(in_6), .en(in_5));
  Multiplexer #(.select(2)) multiplexer_3 (
    .in0(INC_c_2), .in1(main_1_c_2), .in2(main_2_out_7), .in3(in_7), .out(out_10), .sel(in_6), .en(in_5));
  Multiplexer #(.select(2)) multiplexer_4 (
    .in0(INC_d_2), .in1(main_1_d_2), .in2(main_2_out_8), .in3(in_7), .out(out_11), .sel(in_6), .en(in_5));
  TODOS todos_2 (
    .A(out_8), .B(out_9), .C(out_10), .D(out_11), .out_5(todos_2_out_5), .out_6(todos_2_out_6),
    .out_7(todos_2_out_7), .out_8(todos_2_out_8), .out_9(todos_2_out_9), .out_10(todos_2_out_10),
    .out_11(todos_2_out_11));
  _7_Segment_Display #(.active("false")) u_7_segment_display_2 (
    .g(todos_2_out_11), .f(todos_2_out_10), .a(todos_2_out_5), .b(todos_2_out_6), .e(todos_2_out_9),
    .d(todos_2_out_8), .c(todos_2_out_7));  // open: dp

  // Notes on the sheet:
  //   4511
  //   NEG
  //   DEC
  //   4511
endmodule
