// Logisim project 4 bit Adder.circ as structural Verilog: 1 circuit, main circuit main
module main (
  input  A,
  input  B,
  input  C,
  input  D,
  input  A1,
  input  B1,
  input  C1,
  input  D1,
  input  Cin,
  output Cout,
  output A_2,
  output B_2,
  output C_2,
  output D_2
);

  wire main_2_cout, main_3_cout, main_4_cout;

  Full_Adder_main main_1 (.Cin(main_2_cout), .A(A), .B(A1), .S(A_2), .Cout(Cout));
  Full_Adder_main main_2 (.Cin(main_3_cout), .A(B), .B(B1), .S(B_2), .Cout(main_2_cout));
  Full_Adder_main main_3 (.Cin(main_4_cout), .A(C), .B(C1), .S(C_2), .Cout(main_3_cout));
  Full_Adder_main main_4 (.Cin(Cin), .A(D), .B(D1), .S(D_2), .Cout(main_4_cout));
endmodule
