// Logisim project Full Adder.circ as structural Verilog: 1 circuit, main circuit main
module main (
  input  Cin,
  input  A,
  input  B,
  output S,
  output Cout
);

  wire and_1_out, and_2_out, and_3_out, and_4_out, xor_1_out;

  ExactlyOne xor_1 (.out(xor_1_out), .in0(Cin), .in2(A), .in4(B));
  and and_1 (and_1_out, Cin, A, B);
  and and_2 (and_2_out, A, B);
  and and_3 (and_3_out, Cin, A);
  and and_4 (and_4_out, Cin, B);
  or or_1 (S, xor_1_out, and_1_out);
  or or_2 (Cout, and_2_out, and_3_out, and_4_out);
endmodule
