// Logisim project 4 bit Subtractor.circ as structural Verilog: 1 circuit, main circuit main
module main (
  input  A,
  input  B,
  input  C,
  input  D,
  input  A1,
  input  B1,
  input  C1,
  input  D1,
  input  Cin,
  output out_10,
  output out_11,
  output out_12,
  output out_13,
  output out_14
);

  wire main_2_cout, main_3_cout, main_4_cout;

  Full_Subtractor_main main_1 (.A(A), .B(A1), .Cin(main_2_cout), .S(out_11), .Cout(out_10));
  Full_Subtractor_main main_2 (.A(B), .B(B1), .Cin(main_3_cout), .S(out_12), .Cout(main_2_cout));
  Full_Subtractor_main main_3 (.A(C), .B(C1), .Cin(main_4_cout), .S(out_13), .Cout(main_3_cout));
  Full_Subtractor_main main_4 (.A(D), .B(D1), .Cin(Cin), .S(out_14), .Cout(main_4_cout));
endmodule
