// Logisim project Full Subtractor.circ as structural Verilog: 1 circuit, main circuit main
module main (
  input  A,
  input  B,
  input  Cin,
  output S,
  output Cout
);

  wire and_1_out, and_2_out, and_3_out, not_1_out, not_2_out, xor_1_out;

  not not_1 (not_1_out, A);
  not not_2 (not_2_out, A);
  xor xor_1 (xor_1_out, B, Cin);
  and and_1 (and_1_out, not_1_out, B);
  and and_2 (and_2_out, not_2_out, Cin);
  and and_3 (and_3_out, B, Cin);
  xor xor_2 (S, xor_1_out, A);
  or or_1 (Cout, and_1_out, and_2_out, and_3_out);
endmodule
