// Logisim project DEC.circ as structural Verilog: 1 circuit, main circuit main
module main (
  input  A,
  input  B,
  input  C,
  input  D,
  output out_5,
  output out_6,
  output out_7,
  output out_8
);

  wire and_1_out, and_2_out, and_3_out, and_4_out, and_5_out, and_6_out, and_7_out, and_8_out, and_9_out,
       and_10_out, and_11_out, and_12_out, not_1_out, not_2_out, not_3_out, not_4_out, not_5_out, not_6_out,
       not_7_out, not_8_out, not_9_out, not_10_out;

  not not_1 (not_1_out, B);
  not not_2 (not_2_out, C);
  not not_3 (not_3_out, D);
  not not_4 (not_4_out, C);
  not not_5 (not_5_out, D);
  not not_6 (not_6_out, C);
  not not_7 (not_7_out, D);
  not not_8 (not_8_out, D);
  not not_9 (not_9_out, D);
  not not_10 (not_10_out, D);
  and and_1 (and_1_out, A, B);
  and and_2 (and_2_out, A, C);
  and and_3 (and_3_out, A, D);
  and and_4 (and_4_out, A, not_1_out, not_2_out, not_3_out);
  and and_5 (and_5_out, B, C);
  and and_6 (and_6_out, B, D);
  and and_7 (and_7_out, A, not_4_out, not_5_out);
  and and_8 (and_8_out, B, not_6_out, not_7_out);
  and and_9 (and_9_out, C, D);
  and and_10 (and_10_out, A, not_8_out);
  and and_11 (and_11_out, B, not_9_out);
  and and_12 (and_12_out, C, not_10_out);
  or or_1 (out_5, and_1_out, and_2_out, and_3_out);
  or or_2 (out_6, and_4_out, and_5_out, and_6_out);
  or or_3 (out_7, and_7_out, and_8_out, and_9_out);
  or or_4 (out_8, and_10_out, and_11_out, and_12_out);
endmodule
