// Logisim project INC.circ as structural Verilog: 1 circuit, main circuit main
module main (
  input  A,
  input  B,
  input  C,
  input  D,
  output A_2,
  output B_2,
  output C_2,
  output D_2
);

  wire and_1_out, and_2_out, and_3_out, and_4_out, and_5_out, and_6_out, and_7_out, not_1_out, not_2_out,
       not_3_out, not_4_out, not_5_out, not_6_out, not_7_out;

  not not_1 (not_1_out, A);
  not not_2 (not_2_out, B);
  not not_3 (not_3_out, C);
  not not_4 (not_4_out, D);
  not not_5 (not_5_out, B);
  not not_6 (not_6_out, C);
  not not_7 (not_7_out, D);
  xor xor_1 (C_2, C, D);
  not not_8 (D_2, D);
  and and_1 (and_1_out, not_1_out, B, C, D);
  and and_2 (and_2_out, A, not_2_out);
  and and_3 (and_3_out, A, not_3_out);
  and and_4 (and_4_out, A, not_4_out);
  and and_5 (and_5_out, not_5_out, C, D);
  and and_6 (and_6_out, B, not_6_out);
  and and_7 (and_7_out, B, not_7_out);
  or or_1 (A_2, and_1_out, and_2_out, and_3_out, and_4_out);
  or or_2 (B_2, and_5_out, and_6_out, and_7_out);
endmodule
