// Logisim project 7SEG_CATODO.circ as structural Verilog
// A-0
module _0_A (
  input  a,
  input  b,
  input  c,
  input  d,
  output x
);

  wire and_1_out, and_2_out, and_3_out, and_4_out, and_5_out, and_6_out, not_1_out, not_2_out, not_3_out,
       not_4_out, not_5_out, not_6_out, not_7_out;

  not not_1 (not_1_out, b);
  and and_1 (and_1_out, not_1_out, not_2_out);
  not not_2 (not_2_out, d);
  not not_3 (not_3_out, a);
  and and_2 (and_2_out, not_3_out, c);
  not not_4 (not_4_out, a);
  and and_3 (and_3_out, not_4_out, b, d);
  and and_4 (and_4_out, b, c);
  and and_5 (and_5_out, a, not_5_out, not_6_out);
  not not_5 (not_5_out, b);
  not not_6 (not_6_out, c);
  and and_6 (and_6_out, a, not_7_out);
  not not_7 (not_7_out, d);
  or or_1 (x, and_1_out, and_2_out, and_3_out, and_4_out, and_5_out, and_6_out);
endmodule

// B-1
module _1_B (
  input  a,
  input  b,
  input  c,
  input  d,
  output x
);

  wire and_1_out, and_2_out, and_3_out, and_4_out, and_5_out, not_1_out, not_2_out, not_3_out, not_4_out,
       not_5_out, not_6_out, not_7_out, not_8_out, not_9_out;

  not not_1 (not_1_out, a);
  and and_1 (and_1_out, not_1_out, not_2_out);
  not not_2 (not_2_out, b);
  not not_3 (not_3_out, a);
  not not_4 (not_4_out, c);
  and and_2 (and_2_out, not_3_out, not_4_out, not_5_out);
  not not_5 (not_5_out, d);
  not not_6 (not_6_out, b);
  and and_3 (and_3_out, not_6_out, not_7_out);
  not not_7 (not_7_out, d);
  not not_8 (not_8_out, a);
  and and_4 (and_4_out, not_8_out, c, d);
  and and_5 (and_5_out, a, not_9_out, d);
  not not_9 (not_9_out, c);
  or or_1 (x, and_1_out, and_2_out, and_3_out, and_4_out, and_5_out);
endmodule

// C-2
module _2_C (
  input  a,
  input  b,
  input  c,
  input  d,
  output x
);

  wire and_1_out, and_2_out, and_3_out, and_4_out, and_5_out, not_1_out, not_2_out, not_3_out, not_4_out,
       not_5_out, not_6_out;

  not not_1 (not_1_out, a);
  and and_1 (and_1_out, not_1_out, not_2_out);
  not not_2 (not_2_out, c);
  not not_3 (not_3_out, a);
  and and_2 (and_2_out, not_3_out, d);
  not not_4 (not_4_out, c);
  and and_3 (and_3_out, not_4_out, d);
  not not_5 (not_5_out, a);
  and and_4 (and_4_out, not_5_out, b);
  and and_5 (and_5_out, a, not_6_out);
  not not_6 (not_6_out, b);
  or or_1 (x, and_1_out, and_2_out, and_3_out, and_4_out, and_5_out);
endmodule

// D-3
module _3_D (
  input  a,
  input  b,
  input  c,
  input  d,
  output x
);

  wire and_1_out, and_2_out, and_3_out, and_4_out, and_5_out, not_1_out, not_2_out, not_3_out, not_4_out,
       not_5_out, not_6_out, not_7_out;

  not not_1 (not_1_out, a);
  not not_2 (not_2_out, b);
  and and_1 (and_1_out, not_1_out, not_2_out, not_3_out);
  not not_3 (not_3_out, d);
  not not_4 (not_4_out, b);
  and and_2 (and_2_out, not_4_out, c, d);
  not not_5 (not_5_out, c);
  and and_3 (and_3_out, b, not_5_out, d);
  and and_4 (and_4_out, b, c, not_6_out);
  not not_6 (not_6_out, d);
  and and_5 (and_5_out, a, not_7_out);
  not not_7 (not_7_out, c);
  or or_1 (x, and_1_out, and_2_out, and_3_out, and_4_out, and_5_out);
endmodule

// E-4
module _4_E (
  input  a,
  input  b,
  input  c,
  input  d,
  output x
);

  wire and_1_out, and_2_out, and_3_out, and_4_out, not_1_out, not_2_out, not_3_out;

  not not_1 (not_1_out, b);
  and and_1 (and_1_out, not_1_out, not_2_out);
  not not_2 (not_2_out, d);
  and and_2 (and_2_out, c, not_3_out);
  not not_3 (not_3_out, d);
  and and_3 (and_3_out, a, c);
  and and_4 (and_4_out, a, b);
  or or_1 (x, and_1_out, and_2_out, and_3_out, and_4_out);
endmodule

// F-5
module _5_F (
  input  a,
  input  b,
  input  c,
  input  d,
  output x
);

  wire and_1_out, and_2_out, and_3_out, and_4_out, and_5_out, not_1_out, not_2_out, not_3_out, not_4_out,
       not_5_out, not_6_out;

  not not_1 (not_1_out, c);
  and and_1 (and_1_out, not_1_out, not_2_out);
  not not_2 (not_2_out, d);
  not not_3 (not_3_out, a);
  and and_2 (and_2_out, not_3_out, b, not_4_out);
  not not_4 (not_4_out, c);
  and and_3 (and_3_out, b, not_5_out);
  not not_5 (not_5_out, d);
  and and_4 (and_4_out, a, not_6_out);
  not not_6 (not_6_out, b);
  and and_5 (and_5_out, a, c);
  or or_1 (x, and_1_out, and_2_out, and_3_out, and_4_out, and_5_out);
endmodule

// G-6
module _6_G (
  input  a,
  input  b,
  input  c,
  input  d,
  output x
);

  wire and_1_out, and_2_out, and_3_out, and_4_out, and_5_out, not_1_out, not_2_out, not_3_out, not_4_out,
       not_5_out;

  not not_1 (not_1_out, b);
  and and_1 (and_1_out, not_1_out, c);
  and and_2 (and_2_out, c, not_2_out);
  not not_2 (not_2_out, d);
  not not_3 (not_3_out, a);
  and and_3 (and_3_out, not_3_out, b, not_4_out);
  not not_4 (not_4_out, c);
  and and_4 (and_4_out, a, not_5_out);
  not not_5 (not_5_out, b);
  and and_5 (and_5_out, a, d);
  or or_1 (x, and_1_out, and_2_out, and_3_out, and_4_out, and_5_out);
endmodule

module TODOS (
  input  A,
  input  B,
  input  C,
  input  D,
  output out_5,
  output out_6,
  output out_7,
  output out_8,
  output out_9,
  output out_10,
  output out_11
);

  _0_A u_0_a_1 (.a(A), .b(B), .c(C), .d(D), .x(out_5));
  _1_B u_1_b_1 (.a(A), .b(B), .c(C), .d(D), .x(out_6));
  _2_C u_2_c_1 (.a(A), .b(B), .c(C), .d(D), .x(out_7));
  _3_D u_3_d_1 (.a(A), .b(B), .c(C), .d(D), .x(out_8));
  _4_E u_4_e_1 (.a(A), .b(B), .c(C), .d(D), .x(out_9));
  _5_F u_5_f_1 (.a(A), .b(B), .c(C), .d(D), .x(out_10));
  _6_G u_6_g_1 (.a(A), .b(B), .c(C), .d(D), .x(out_11));
endmodule

module _7SEG (
  input  in_1,
  input  in_2,
  input  in_3,
  input  in_4
);

  wire todos_1_out_5, todos_1_out_6, todos_1_out_7, todos_1_out_8, todos_1_out_9, todos_1_out_10,
       todos_1_out_11;

  TODOS todos_1 (
    .A(in_1), .B(in_2), .C(in_3), .D(in_4), .out_5(todos_1_out_5), .out_6(todos_1_out_6),
    .out_7(todos_1_out_7), .out_8(todos_1_out_8), .out_9(todos_1_out_9), .out_10(todos_1_out_10),
    .out_11(todos_1_out_11));
  _7_Segment_Display u_7_segment_display_1 (
    .g(todos_1_out_11), .f(todos_1_out_10), .a(todos_1_out_5), .b(todos_1_out_6), .e(todos_1_out_9),
    .d(todos_1_out_8), .c(todos_1_out_7));  // open: dp

  // Notes on the sheet:
  //   4511
endmodule
