// Logisim project B.circ as structural Verilog: 1 circuit, main circuit main
module main (
  input  A,
  input  B,
  input  C,
  input  D,
  input  E,
  input  F,
  output out_7
);

  wire and_1_out, and_2_out, and_3_out, and_4_out, not_1_out, not_2_out, not_3_out, not_4_out;

  not not_1 (not_1_out, B);
  not not_2 (not_2_out, B);
  not not_3 (not_3_out, C);
  not not_4 (not_4_out, D);
  and and_1 (and_1_out, not_1_out, C, E);
  and and_2 (and_2_out, not_2_out, C, D);
  and and_3 (and_3_out, C, D, E);
  and and_4 (and_4_out, B, not_3_out, not_4_out);
  or or_1 (out_7, A, and_1_out, and_2_out, and_3_out, and_4_out);
endmodule
