// Logisim project C.circ as structural Verilog: 1 circuit, main circuit main
module main (
  input  A,
  input  B,
  input  C,
  input  D,
  input  E,
  input  F,
  output out_7
);

  wire and_1_out, and_2_out, and_3_out, and_4_out, not_1_out, not_2_out, not_3_out, not_4_out, not_5_out,
       not_6_out;

  not not_1 (not_1_out, B);
  not not_2 (not_2_out, D);
  not not_3 (not_3_out, E);
  not not_4 (not_4_out, C);
  not not_5 (not_5_out, D);
  not not_6 (not_6_out, E);
  and and_1 (and_1_out, A, D, E);
  and and_2 (and_2_out, not_1_out, C, not_2_out, not_3_out);
  and and_3 (and_3_out, B, not_4_out, not_5_out, E);
  and and_4 (and_4_out, B, C, D, not_6_out);
  or or_1 (out_7, and_1_out, and_2_out, and_3_out, and_4_out);
endmodule
