// Logisim project D.circ as structural Verilog: 1 circuit, main circuit main
module main (
  input  A,
  input  B,
  input  C,
  input  D,
  input  E,
  input  F,
  output out_7
);

  wire and_1_out, and_2_out, and_3_out, and_4_out, and_5_out, not_1_out, not_2_out, not_3_out, not_4_out,
       not_5_out, not_6_out, not_7_out, not_8_out, not_9_out;

  not not_1 (not_1_out, D);
  not not_2 (not_2_out, D);
  not not_3 (not_3_out, E);
  not not_4 (not_4_out, D);
  not not_5 (not_5_out, A);
  not not_6 (not_6_out, B);
  not not_7 (not_7_out, B);
  not not_8 (not_8_out, C);
  not not_9 (not_9_out, E);
  and and_1 (and_1_out, A, not_1_out, E);
  and and_2 (and_2_out, B, not_2_out, not_3_out);
  and and_3 (and_3_out, B, C, not_4_out);
  and and_4 (and_4_out, not_5_out, not_6_out, D, E);
  and and_5 (and_5_out, not_7_out, not_8_out, D, not_9_out);
  or or_1 (out_7, and_1_out, and_2_out, and_3_out, and_4_out, and_5_out);
endmodule
