// Logisim project E.circ as structural Verilog: 1 circuit, main circuit main
module main (
  input  A,
  input  B,
  input  C,
  input  D,
  input  E,
  input  F,
  output out_7
);

  wire and_1_out, and_2_out, and_3_out, and_4_out, and_5_out, and_6_out, not_1_out, not_2_out, not_3_out,
       not_4_out, not_5_out, not_6_out, not_7_out, not_8_out, not_9_out, not_10_out, not_11_out, not_12_out,
       or_1_out, or_2_out;

  not not_1 (not_1_out, E);
  not not_2 (not_2_out, A);
  not not_3 (not_3_out, B);
  not not_4 (not_4_out, C);
  not not_5 (not_5_out, A);
  not not_6 (not_6_out, C);
  not not_7 (not_7_out, B);
  not not_8 (not_8_out, E);
  not not_9 (not_9_out, C);
  not not_10 (not_10_out, D);
  not not_11 (not_11_out, E);
  not not_12 (not_12_out, D);
  and and_1 (and_1_out, A, not_1_out);
  and and_2 (and_2_out, not_2_out, not_3_out, not_4_out, E);
  and and_3 (and_3_out, not_5_out, not_6_out, D, E);
  and and_4 (and_4_out, not_7_out, C, D, not_8_out);
  and and_5 (and_5_out, B, not_9_out, not_10_out, not_11_out);
  and and_6 (and_6_out, B, C, not_12_out, E);
  or or_1 (or_1_out, and_1_out, and_2_out, and_3_out);
  or or_2 (or_2_out, and_4_out, and_5_out, and_6_out);
  or or_3 (out_7, or_1_out, or_2_out);
endmodule
