// Logisim project Ex3.circ as structural Verilog: 1 circuit, main circuit main
module main (
  input  A,
  input  B,
  input  C,
  input  D,
  input  E,
  input  F,
  input  in_7,
  output out_8,
  output out_9,
  output out_10,
  output out_11,
  output out_12,
  output out_13
);

  wire todos_1_out_5, todos_1_out_6, todos_1_out_7, todos_1_out_8, todos_1_out_9, todos_1_out_10,
       todos_1_out_11, todos_2_out_5, todos_2_out_6, todos_2_out_7, todos_2_out_8, todos_2_out_9,
       todos_2_out_10, todos_2_out_11;

  A_main main_1 (.A(A), .B(B), .C(C), .D(D), .E(E), .F(F), .out_7(out_8));
  B_main main_2 (.A(A), .B(B), .C(C), .D(D), .E(E), .F(F), .out_7(out_9));
  C_main main_3 (.A(A), .B(B), .C(C), .D(D), .E(E), .F(F), .out_7(out_10));
  D_main main_4 (.A(A), .B(B), .C(C), .D(D), .E(E), .F(F), .out_7(out_11));
  E_main main_5 (.A(A), .B(B), .C(C), .D(D), .E(E), .F(F), .out_7(out_12));
  F_main main_6 (.A(A), .B(B), .C(C), .D(D), .E(E), .F(F), .out_7(out_13));
  TODOS todos_1 (
    .A(in_7), .B(in_7), .C(out_8), .D(out_9), .out_5(todos_1_out_5), .out_6(todos_1_out_6),
    .out_7(todos_1_out_7), .out_8(todos_1_out_8), .out_9(todos_1_out_9), .out_10(todos_1_out_10),
    .out_11(todos_1_out_11));
  TODOS todos_2 (
    .A(out_10), .B(out_11), .C(out_12), .D(out_13), .out_5(todos_2_out_5), .out_6(todos_2_out_6),
    .out_7(todos_2_out_7), .out_8(todos_2_out_8), .out_9(todos_2_out_9), .out_10(todos_2_out_10),
    .out_11(todos_2_out_11));
  _7_Segment_Display u_7_segment_display_1 (
    .g(todos_2_out_11), .f(todos_2_out_10), .a(todos_2_out_5), .b(todos_2_out_6), .e(todos_2_out_9),
    .d(todos_2_out_8), .c(todos_2_out_7));  // open: dp
  _7_Segment_Display u_7_segment_display_2 (
    .g(todos_1_out_11), .f(todos_1_out_10), .a(todos_1_out_5), .b(todos_1_out_6), .e(todos_1_out_9),
    .d(todos_1_out_8), .c(todos_1_out_7));  // open: dp

  // Notes on the sheet:
  //   4511
  //   4511
endmodule
